# Fritzing sketch SoilMoistureHeader (saved by Fritzing 0.9.3b)
circuit board: 3.9cm x 5.6cm
breadboards: 1

parts:
  +Motor- = DC Motor
  Diode = Rectifier Diode [part_number=1N4001 package="300 mil [THT]"]
  R3 = Resistor [tolerance=±5% resistance=1k package=THT]
  R1 = Resistor [tolerance=±5% resistance=1k package=THT]
  R2 = Resistor [tolerance=±5% resistance=1k package=THT]
  ADC = rounded female pin header, 4 pins [form="♀ (female rounded)"]
  Daniel_Bujold = rounded female pin header, 2 pins [form="♀ (female rounded)"]
  Switch = rounded female pin header, 5 pins [form="♀ (female rounded)"]
  +Sensor- = Gikfun
  NPN = NPN-Transistor [package="TO92 [THT]"]
  12V_Jack = Power Jack [package=power_jack_pth]
  Pi = rounded female pin header, 9 pins [form="♀ (female rounded)"]

nets:
  N1: +Motor-.pin_1, Diode.cathode, 12V_Jack.PWR
  N2: +Motor-.pin_2, Diode.anode, NPN.C
  N3: R3.Pin_0, NPN.B
  N4: R3.Pin_1, Pi.pin2
  N5: R1.Pin_0, R2.Pin_1, Switch.pin4
  N6: R1.Pin_1, +Sensor-.VCC, Pi.pin1
  GND: R2.Pin_0, ADC.pin3, Switch.pin5, +Sensor-.GND, NPN.E, 12V_Jack.GND, 12V_Jack.GNDBREAK, Pi.pin5
  N7: ADC.pin1, Pi.pin8
  N8: ADC.pin2, Pi.pin7
  N9: ADC.pin4, Switch.pin1, Pi.pin9
  N10: Daniel_Bujold.pin1, Switch.pin3
  N11: Daniel_Bujold.pin2, +Sensor-.OUT

notes:
  D. Bujold
  Lo
  Med
  Hi

custom parts:
  Gikfun: Gikfun - Capacitive soil moisture sensor
