# Fritzing sketch useforPCB (saved by Fritzing 0.9.3b)
circuit board: 4.4cm x 5.6cm
breadboards: 1

parts:
  +Motor- = DC Motor
  Diode = Rectifier Diode [part_number=1N4001 package="300 mil [THT]"]
  Lo = Resistor [tolerance=±5% resistance=1k package=THT]
  R1 = Resistor [tolerance=±5% resistance=1k package=THT]
  R2 = Resistor [tolerance=±5% resistance=1k package=THT]
  ADC = rounded female pin header, 4 pins [form="♀ (female rounded)"]
  Daniel_Bujold = rounded female pin header, 2 pins [form="♀ (female rounded)"]
  Switch = rounded female pin header, 5 pins [form="♀ (female rounded)"]
  +Sensor- = Gikfun
  Q1 = NPN-Transistor [package="TO92 [THT]"]
  Pi = double row rounded female pin header, 28 pins [form="♀ (female rounded)"]

nets:
  N1: +Motor-.pin_1, Diode.cathode, Pi.pin14
  N2: +Motor-.pin_2, Diode.anode, Q1.C
  N3: Lo.Pin_0, Pi.pin24
  N4: Lo.Pin_1, Q1.B
  N5: R1.Pin_0, R2.Pin_1, Switch.pin4
  N6: R1.Pin_1, ADC.pin4, Switch.pin1, Pi.pin15
  N7: R2.Pin_0, Switch.pin5, Pi.pin27
  N8: ADC.pin1, Pi.pin16
  N9: ADC.pin2, Pi.pin17
  N10: ADC.pin3, +Sensor-.GND, Q1.E, Pi.pin19
  N11: Daniel_Bujold.pin1, Switch.pin3
  N12: Daniel_Bujold.pin2, +Sensor-.OUT
  N13: +Sensor-.VCC, Pi.pin23

notes:
  Daniel Bujold
  Lo
  Med
  Hi

custom parts:
  Gikfun: Gikfun - Capacitive soil moisture sensor
